// Logisim project ALU.circ as structural Verilog: 5 circuits, main circuit ALU
module ALU (
  input  [31:0] in_1,
  input  [31:0] in_2,
  input  [3:0] in_3,
  output [31:0] out_4,
  output [31:0] out_5
);

  wire comparator_1_lt, comparator_2_lt;
  wire [31:0] add, \and , divHi, divLo, divuHi, divuLo, multHi, multLo, muluHi, muluLo, \nor , \or ,
       signed_div_1_out_3, signed_div_1_out_4, slt, stlu, sub, \xor ;

  Adder #(.width(32)) adder_1 (.a(in_1), .b(in_2), .out(add));  // open: cin, cout
  Subtractor #(.width(32)) subtractor_1 (.a(in_1), .b(in_2), .out(sub));  // open: bin, bout
  Multiplier #(.width(32)) multiplier_1 (.a(in_1), .b(in_2), .out(muluLo), .cout(muluHi));  // open: cin
  Divider #(.width(32)) divider_1 (.a(in_1), .b(in_2), .out(divuLo), .rem(divuHi));  // open: upper
  Signed_Mult signed_mult_1 (.in_1(in_1), .in_2(in_2), .out_3(multLo), .out_4(multHi));
  Signed_Div signed_div_1 (.in_1(in_1), .in_2(in_2), .out_3(signed_div_1_out_3), .out_4(signed_div_1_out_4));
  assign \and  = in_1 & in_2;  // AND_Gate and_1, 32 bits wide
  assign \or  = in_1 | in_2;  // OR_Gate or_1, 32 bits wide
  assign \nor  = ~(in_1 | in_2);  // NOR_Gate nor_1, 32 bits wide
  assign \xor  = in_1 ^ in_2;  // XOR_Gate xor_1, 32 bits wide
  Multiplexer #(.select(4), .width(32), .enable("false")) multiplexer_1 (
    .in0(add), .in1(sub), .in2(multLo), .in3(muluLo), .in4(divLo), .in5(divuLo), .in6(\and ), .in7(\or ),
    .in8(\nor ), .out(out_4), .sel(in_3));  // open: in9, in10, in11, in12, in13, in14, in15
  Multiplexer #(.select(2), .width(32), .disabled(0), .enable("false")) multiplexer_2 (
    .in0(divHi), .in1(divuHi), .in2(multHi), .in3(muluHi), .out(out_5), .sel(in_3[1:0]));
  Comparator #(.width(32)) comparator_1 (.a(in_1), .b(in_2), .lt(comparator_1_lt));  // open: gt, eq
  Comparator #(.width(32), .mode("unsigned")) comparator_2 (.a(in_1), .b(in_2), .lt(comparator_2_lt));  // open: gt, eq
  assign slt = {{31{1'b0}}, comparator_1_lt};  // Bit_Extender bit_extender_1
  assign stlu = {{31{1'b0}}, comparator_2_lt};  // Bit_Extender bit_extender_2

  // Other names for the same wires on the sheet: A[31:0] = in_1; B[31:0] = in_2; High[31:0] = out_5;
  //   Hi_select[1:0] = in_3[1:0]; Op[3:0] = in_3; R[31:0] = out_4

  // Notes on the sheet:
  //   Arithmetics
  //   Inputs
  //   Logics
  //   ALU
  //   Comparison
  //   Outputs
endmodule

module Signed_Mult (
  input  [31:0] in_1,
  input  [31:0] in_2,
  output [31:0] out_3,
  output [31:0] out_4
);

  wire Sign, Sign_A, Sign_B, to_negative_1_carry_out;
  wire [31:0] adder_1_out, multiplier_1_cout, multiplier_1_out, not_1_out, to_negative_1_out_2,
       to_positive_1_out_2, to_positive_2_out_2;

  xor xor_1 (Sign, Sign_A, Sign_B);
  // Probe on in_1
  // Probe on in_2
  To_Positive to_positive_1 (.in_1(in_1), .out_2(to_positive_1_out_2), .Input_sign(Sign_A));
  To_Positive to_positive_2 (.in_1(in_2), .out_2(to_positive_2_out_2), .Input_sign(Sign_B));
  Multiplier #(.width(32)) multiplier_1 (
    .a(to_positive_1_out_2), .b(to_positive_2_out_2), .out(multiplier_1_out), .cout(multiplier_1_cout));  // open: cin
  assign not_1_out = ~multiplier_1_cout;  // NOT_Gate not_1, 32 bits wide
  To_Negative to_negative_1 (.in_1(multiplier_1_out), .out_2(to_negative_1_out_2), .Carry_out(to_negative_1_carry_out));
  Adder #(.width(32)) adder_1 (
    .a({32{1'b0}}), .b(not_1_out), .out(adder_1_out), .cin(to_negative_1_carry_out));  // open: cout
  Multiplexer #(.width(32), .disabled(0), .enable("false")) multiplexer_1 (
    .in0(multiplier_1_out), .in1(to_negative_1_out_2), .out(out_3), .sel(Sign));
  Multiplexer #(.width(32), .disabled(0), .enable("false")) multiplexer_2 (
    .in0(adder_1_out), .in1(multiplier_1_cout), .out(out_4), .sel(Sign));
  // Probe on out_3
  // Probe on out_4

  // Notes on the sheet:
  //   A
  //   B
  //   Mult
  //   Low
  //   High
endmodule

module Signed_Div (
  input  [31:0] in_1,
  input  [31:0] in_2,
  output [31:0] out_3,
  output [31:0] out_4
);

  wire Sign, Sign_A, Sign_B;
  wire [31:0] divider_1_out, divider_1_rem, to_negative_1_out_2, to_negative_2_out_2, to_positive_1_out_2,
       to_positive_2_out_2;

  xor xor_1 (Sign, Sign_A, Sign_B);
  // Probe on in_1
  // Probe on in_2
  To_Positive to_positive_1 (.in_1(in_1), .out_2(to_positive_1_out_2), .Input_sign(Sign_A));
  To_Positive to_positive_2 (.in_1(in_2), .out_2(to_positive_2_out_2), .Input_sign(Sign_B));
  Divider #(.width(32)) divider_1 (
    .a(to_positive_1_out_2), .b(to_positive_2_out_2), .out(divider_1_out), .rem(divider_1_rem));  // open: upper
  To_Negative to_negative_1 (.in_1(divider_1_out), .out_2(to_negative_1_out_2));  // open: Carry_out
  To_Negative to_negative_2 (.in_1(divider_1_rem), .out_2(to_negative_2_out_2));  // open: Carry_out
  Multiplexer #(.width(32), .disabled(0), .enable("false")) multiplexer_1 (
    .in0(divider_1_out), .in1(to_negative_1_out_2), .out(out_3), .sel(Sign));
  Multiplexer #(.width(32), .disabled(0), .enable("false")) multiplexer_2 (
    .in0(divider_1_rem), .in1(to_negative_2_out_2), .out(out_4), .sel(Sign));
  // Probe on out_3
  // Probe on out_4

  // Notes on the sheet:
  //   A
  //   B
  //   Div
  //   Low
  //   High
endmodule

module To_Negative (
  input  [31:0] in_1,
  output [31:0] out_2,
  output Carry_out
);

  wire [31:0] not_1_out;

  // Probe on in_1
  assign not_1_out = ~in_1;  // NOT_Gate not_1, 32 bits wide
  // Probe on out_2
  Adder #(.width(32)) adder_1 (.a(not_1_out), .b(32'h1), .out(out_2), .cout(Carry_out));  // open: cin

  // Notes on the sheet:
  //   Input
  //   Opposite
  //   Output
endmodule

module To_Positive (
  input  [31:0] in_1,
  output [31:0] out_2,
  output Input_sign
);

  wire [31:0] to_negative_1_out_2;

  // Probe on in_1
  To_Negative to_negative_1 (.in_1(in_1), .out_2(to_negative_1_out_2));  // open: Carry_out
  // Probe on out_2
  Multiplexer #(.width(32), .disabled(0), .enable("false")) multiplexer_1 (
    .in0(in_1), .in1(to_negative_1_out_2), .out(out_2), .sel(in_1[31]));

  assign Input_sign = in_1[31];

  // Notes on the sheet:
  //   Input
  //   Abs
  //   Output
endmodule
