// Logisim project Branch Control.circ as structural Verilog: 1 circuit, main circuit Branch Control
module Branch_Control (
  input  [31:0] in_1,
  input  [31:0] in_2,
  input  [31:0] in_3,
  input  [25:0] in_4,
  input  [15:0] in_5,
  input  [2:0] Fag_Condition,
  input  [1:0] Jump_Selector,
  output [31:0] out_8
);

  wire beq, bgtz, blez, bltz, bne, comparator_2_eq, multiplexer_1_out;
  wire [31:0] multiplexer_2_out, PC___4, PC___4___4_x_offset;
  wire [31:18] _4_x_offset;

  Comparator #(.width(32)) comparator_1 (.a(in_1), .b(in_2), .eq(beq));  // open: gt, lt
  Comparator #(.width(32)) comparator_2 (.a(in_1), .b({32{1'b0}}), .gt(bgtz), .eq(comparator_2_eq), .lt(bltz));
  Adder #(.width(32)) adder_1 (.a(in_3), .b(32'h4), .out(PC___4));  // open: cin, cout
  assign _4_x_offset = {{13{in_5[15]}}, in_5[15]};  // Bit_Extender bit_extender_1
  Adder #(.width(32)) adder_2 (
    .a(PC___4), .b({_4_x_offset, in_5, 2'b00}), .out(PC___4___4_x_offset));  // open: cin, cout
  not not_1 (bne, beq);
  or or_1 (blez, comparator_2_eq, bltz);
  Multiplexer #(.select(3), .disabled(0), .enable("false")) multiplexer_1 (
    .in0(beq), .in1(bne), .in2(bgtz), .in3(blez), .in4(bltz), .out(multiplexer_1_out), .sel(Fag_Condition));  // open: in5, in6, in7
  Multiplexer #(.width(32), .disabled(0), .enable("false")) multiplexer_2 (
    .in0(PC___4), .in1(PC___4___4_x_offset), .out(multiplexer_2_out), .sel(multiplexer_1_out));
  Multiplexer #(.select(2), .width(32), .disabled(0), .enable("false")) multiplexer_3 (
    .in0(PC___4), .in1(multiplexer_2_out), .in2({in_3[31:28], in_4, 2'b00}), .in3(in_1), .out(out_8),
    .sel(Jump_Selector));

  // Other names for the same wires on the sheet: _4_x_offset[17:2] = in_5; offset[15:0] = in_5;
  //   Flag_Condition[2:0] = Fag_Condition; dest[25:0] = in_4; jmp[31:2] = {in_3[31:28], in_4}; PC[31:0] = in_3;
  //   PC_in[31:0] = out_8; Rs[31:0] = in_1; Rt[31:0] = in_2; Selector[1:0] = Jump_Selector

  // Notes on the sheet:
  //   Input
  //   [RS]
  //   [RT]
  //   Instruction Address
  //   Unconditional Jump Destiny
  //   Conditional Jump Destiny
  //   Branch Control
  //   Output
  //   Next Instruction Address
endmodule
