// Logisim project Control Unit.circ as structural Verilog: 1 circuit, main circuit Control Unit
module Control_Unit (
  input  reset,
  input  is_read,
  input  is_write,
  input  ready_read,
  input  ready_write,
  input  is_kbd,
  input  is_tty,
  input  is_RF,
  input  halt,
  input  clk,
  input  hi_lo,
  output out_12,
  output out_13,
  output out_14,
  output out_15,
  output out_16,
  output out_17,
  output out_18,
  output out_19,
  output out_20,
  output out_21
);

  wire d_ff_1_q, d_ff_2_q, d_ff_3_q, d_ff_4_q, d_ff_5_q, d_ff_6_q, demultiplexer_2_out0,
       demultiplexer_2_out1, demultiplexer_3_out0, demultiplexer_3_out1, demultiplexer_5_out0,
       demultiplexer_6_out3, end_read, end_write, get_data_1, get_data_2, is_jump, mem, multiplexer_1_out,
       not_1_out, or_1_out, or_2_out, PC, Ram_instr, RF, RF_t;
  wire [1:0] exe;

  Demultiplexer #(.disabled(0), .enable("false")) demultiplexer_1 (
    .out0(get_data_2), .out1(out_13), .in(mem), .sel(is_write));
  or or_1 (or_1_out, demultiplexer_2_out0, reset);
  D_Flip_Flop d_ff_1 (.clk(clk), .D(or_1_out), .Q(d_ff_1_q));  // open: Qn, preset, en, reset
  Demultiplexer #(.disabled(0), .enable("false")) demultiplexer_2 (
    .out0(demultiplexer_2_out0), .out1(demultiplexer_2_out1), .in(d_ff_1_q), .sel(not_1_out));
  not not_1 (not_1_out, reset);
  or or_2 (or_2_out, demultiplexer_3_out0, mem);
  or or_3 (get_data_1, out_17, demultiplexer_2_out1);
  D_Flip_Flop d_ff_2 (.clk(clk), .D(or_2_out), .Q(d_ff_2_q), .reset(reset));  // open: Qn, preset, en
  or or_4 (out_12, get_data_1, get_data_2);
  Demultiplexer #(.disabled(0), .enable("false")) demultiplexer_3 (
    .out0(demultiplexer_3_out0), .out1(demultiplexer_3_out1), .in(d_ff_2_q), .sel(multiplexer_1_out));
  Multiplexer #(.disabled(0), .enable("false")) multiplexer_1 (
    .in0(ready_read), .in1(ready_write), .out(multiplexer_1_out), .sel(is_write));
  or or_5 (Ram_instr, is_read, is_write);
  or or_6 (out_19, demultiplexer_5_out0, get_data_1);
  Demultiplexer #(.disabled(0), .enable("false")) demultiplexer_4 (
    .out0(end_read), .out1(end_write), .in(demultiplexer_3_out1), .sel(is_write));
  nor nor_1 (is_jump, Ram_instr, is_RF);
  and and_1 (out_15, is_kbd, out_17);
  Demultiplexer #(.disabled(0), .enable("false")) demultiplexer_5 (
    .out0(demultiplexer_5_out0), .out1(out_18), .in(d_ff_3_q), .sel(ready_read));
  D_Flip_Flop d_ff_3 (.clk(clk), .D(out_19), .Q(d_ff_3_q), .reset(reset));  // open: Qn, preset, en
  and and_2 (out_14, out_17, is_tty);
  Priority_Encoder #(.select(2)) priority_encoder_1 (
    .in0(is_RF), .in1(Ram_instr), .in2(is_jump), .in3(halt), .out(exe), .en_in(1'b1));  // open: gs, en_out
  D_Flip_Flop d_ff_4 (.clk(clk), .D(out_18), .Q(d_ff_4_q), .reset(reset));  // open: Qn, preset, en
  Demultiplexer #(.select(2), .disabled(0), .enable("false")) demultiplexer_6 (
    .out0(RF), .out1(mem), .out2(PC), .out3(demultiplexer_6_out3), .in(d_ff_4_q), .sel(exe));
  and and_3 (out_21, hi_lo, out_17);
  or or_7 (out_20, d_ff_5_q, demultiplexer_6_out3);
  D_Flip_Flop d_ff_5 (.clk(clk), .D(out_20), .Q(d_ff_5_q), .reset(reset));  // open: Qn, preset, en
  or or_8 (out_16, end_read, RF_t);
  D_Flip_Flop d_ff_6 (.clk(clk), .D(out_16), .Q(d_ff_6_q), .reset(reset));  // open: Qn, preset, en
  or or_9 (out_17, d_ff_6_q, PC, end_write);

  // Other names for the same wires on the sheet: end = out_20; get_data = out_12; hi_lo_en = out_21; IM_en = out_18;
  //   is_inst = out_19; kbd_en = out_15; ready_to_read = ready_read; ready_to_write = ready_write; RF_en = out_16;
  //   tty_en = out_14; Hi_Lo_t = out_17; kbd_clear = out_17; next_inst = out_17; PC_en = out_17; tty_out = out_17;
  //   use_hi_lo = hi_lo; write_data = out_13

  // Notes on the sheet:
  //   Inputs
  //   Wait for RAM
  //   Control Unit
  //   Fetch Instruction
  //   Outputs
  //   Get Next Instruction
endmodule
