// Logisim project Data Path.circ as structural Verilog: 1 circuit, main circuit Data Path
module Data_Path (
  input  in_1,
  input  [31:0] in_2,
  input  [31:0] in_3,
  input  [6:0] in_4,
  input  in_5,
  input  in_6,
  input  in_7,
  input  in_8,
  input  in_9,
  input  in_10,
  output [31:0] out_11,
  output [31:0] out_12,
  output [31:0] out_13,
  output out_14,
  output out_15,
  output out_16,
  output out_17,
  output out_18,
  output out_19,
  output [6:0] out_20,
  output [1:0] out_21
);

  wire instruction_decoder_1_out_4, instruction_decoder_1_out_5, instruction_decoder_1_out_11,
       instruction_decoder_1_out_25, pop, push, sw;
  wire [1:0] BC_selector;
  wire [2:0] Flag_Condition, instruction_decoder_1_out_10;
  wire [3:0] instruction_decoder_1_out_3;
  wire [4:0] instruction_decoder_1_out_9, instruction_decoder_1_selector_a, instruction_decoder_1_selector_b;
  wire [15:0] offset;
  wire [25:0] Dest;
  wire [31:0] alu_1_out_5, alu_input_1_out_5, hi_lo_1_out_5, hi_lo_1_out_6, instruction_memory_1_out_5,
       program_counter_1_p1, program_counter_1_p5, register_file_input_1_out_9, Rt, Rt_t;
  wire [31:7] Rs;

  Instruction_Memory instruction_memory_1 (
    .in_1(in_2), .out_5(instruction_memory_1_out_5), .en(in_8), .clk(in_10), .reset(in_9));
  Instruction_Decoder instruction_decoder_1 (
    .in_1(instruction_memory_1_out_5), .in_2(in_1), .out_3(instruction_decoder_1_out_3),
    .out_4(instruction_decoder_1_out_4), .out_5(instruction_decoder_1_out_5), .BC_jump_Selector(BC_selector),
    .Flag_Condition(Flag_Condition), .out_8(out_18), .out_9(instruction_decoder_1_out_9),
    .out_10(instruction_decoder_1_out_10), .out_11(instruction_decoder_1_out_11),
    .Selector_A(instruction_decoder_1_selector_a), .Selector_B(instruction_decoder_1_selector_b),
    .out_14(offset), .out_15(Dest), .out_16(out_15), .out_17(out_14), .out_18(out_21), .Stop_program(out_17),
    .out_20(out_19), .save_word(sw), .keyboard(out_16), .pop(pop), .push(push),
    .out_25(instruction_decoder_1_out_25));
  // Program_Counter program_counter_1: pin names not known; wires that end beside it: program_counter_1_p1, in_7, in_10, in_9, program_counter_1_p5
  // Probe on program_counter_1_p5
  // Probe on program_counter_1_p1
  // Probe on instruction_decoder_1_selector_b
  // Probe on instruction_decoder_1_selector_a
  // Probe on hi_lo_1_out_5
  // Probe on instruction_decoder_1_out_9
  // Probe on offset
  Register_File_Input register_file_input_1 (
    .RF_Selector(instruction_decoder_1_out_10), .in_2(out_11), .in_3(in_10), .in_4(in_3),
    .in_5(hi_lo_1_out_5), .in_6(hi_lo_1_out_6), .Keyboard(in_4), .in_8(in_5),
    .out_9(register_file_input_1_out_9));
  // Probe on register_file_input_1_out_9
  Branch_Control branch_control_1 (
    .in_1({Rs, out_20}), .in_2(Rt_t), .in_3(program_counter_1_p5), .in_4(Dest), .in_5(offset),
    .Fag_Condition(Flag_Condition), .Jump_Selector(BC_selector), .out_8(program_counter_1_p1));
  // Probe on hi_lo_1_out_6
  // Register_File register_file_1: pin names not known; wires that end beside it: register_file_input_1_out_9, instruction_decoder_1_out_9, in_6, in_9, pop, push, in_10, instruction_decoder_1_selector_a, instruction_decoder_1_selector_b, {Rs, out_20}, Rt, out_12
  // Probe on {Rs, out_20}
  // Probe on Rt
  ALU_Input alu_input_1 (
    .in_1(Rt), .constant(instruction_decoder_1_out_5), .in_3(offset),
    .Is_Inmediate(instruction_decoder_1_out_11), .out_5(alu_input_1_out_5));
  // Probe on alu_input_1_out_5
  // Probe on out_11
  ALU alu_1 (
    .in_1({Rs, out_20}), .in_2(alu_input_1_out_5), .in_3(instruction_decoder_1_out_3), .out_4(out_11),
    .out_5(alu_1_out_5));
  Multiplexer #(.width(32), .disabled(0), .enable("false")) multiplexer_1 (
    .in0({Rs, out_20}), .in1(Rt_t), .out(out_13), .sel(sw));
  Hi_Lo hi_lo_1 (
    .in_1(out_11), .in_2(alu_1_out_5), .in_3(instruction_decoder_1_out_4), .in_4(in_10),
    .out_5(hi_lo_1_out_5), .out_6(hi_lo_1_out_6));

  // Other names for the same wires on the sheet: ALU_output[31:0] = out_11; clk = in_10; halt = out_17; IM_en = in_8;
  //   instruction[31:0] = in_2; is_inst = in_1; jump = out_18; kbd = out_16; KBD_avail = in_5; KBD_data[6:0] = in_4;
  //   MA_input_select[1:0] = out_21; PC_en = in_7; RAM_data[31:0] = in_3; RAM_input[31:0] = out_13; read_R = out_15;
  //   reset = in_9; RF_R_W = in_6; Rs[6:0] = out_20; TTY_DATA[6:0] = out_20; SP[31:0] = out_12; tty = out_19;
  //   write_R = out_14

  // Notes on the sheet:
  //   Inputs
  //   Data Path
  //   Outputs
endmodule
