// Logisim project Instruction Decoder.circ as structural Verilog: 10 circuits, main circuit Op-ALU
module Instruction_Decoder (
  input  [31:0] in_1,
  input  in_2,
  output [3:0] out_3,
  output out_4,
  output [4:0] Selector_A,
  output [2:0] out_6,
  output out_7,
  output [4:0] Selector_B,
  output [1:0] out_9,
  output [4:0] out_10,
  output out_11,
  output [1:0] BC_jump_Selector,
  output out_13,
  output [15:0] out_14,
  output [2:0] Flag_Condition,
  output save_word,
  output [25:0] out_17,
  output pop,
  output out_19,
  output push,
  output out_21,
  output keyboard,
  output out_23,
  output Stop_program
);

  wire _0_op, _1_op, add, addi, \and , andi, beq, bgtz, blez, bltz, bne, comparator_1_eq, comparator_2_eq,
       comparator_3_eq, comparator_4_eq, comparator_5_eq, comparator_6_eq, comparator_7_eq, comparator_8_eq,
       comparator_9_eq, comparator_10_eq, comparator_11_eq, comparator_12_eq, comparator_26_eq,
       comparator_27_eq, comparator_31_eq, comparator_32_eq, comparator_33_eq, comparator_34_eq,
       comparator_36_eq, comparator_37_eq, comparator_38_eq, comparator_39_eq, div, divu, en_jump, j, jr, lw,
       mfhi, mflo, mult, mulu, nop, \nor , nor_1_out, \or , ori, rnd, slt, slti, sltiu, sltu, stack_op, sub,
       \xor , xori;

  // Probe on 6'b100000
  // Probe on 6'b100010
  // Probe on 6'b011000
  // Probe on 6'b011001
  // Probe on 6'b011010
  // Probe on 6'b011011
  Comparator #(.width(6)) comparator_1 (.a(in_1[5:0]), .b(6'b100000), .eq(comparator_1_eq));  // open: gt, lt
  Comparator #(.width(6)) comparator_2 (.a(in_1[5:0]), .b(6'b100010), .eq(comparator_2_eq));  // open: gt, lt
  Comparator #(.width(6)) comparator_3 (.a(in_1[5:0]), .b(6'b011000), .eq(comparator_3_eq));  // open: gt, lt
  Comparator #(.width(6)) comparator_4 (.a(in_1[5:0]), .b(6'b011001), .eq(comparator_4_eq));  // open: gt, lt
  Comparator #(.width(6)) comparator_5 (.a(in_1[5:0]), .b(6'b011010), .eq(comparator_5_eq));  // open: gt, lt
  Comparator #(.width(6)) comparator_6 (.a(in_1[5:0]), .b(6'b011011), .eq(comparator_6_eq));  // open: gt, lt
  and and_1 (add, _0_op, comparator_1_eq);
  and and_2 (sub, _0_op, comparator_2_eq);
  and and_3 (mult, _0_op, comparator_3_eq);
  and and_4 (mulu, _0_op, comparator_4_eq);
  and and_5 (div, _0_op, comparator_5_eq);
  and and_6 (divu, _0_op, comparator_6_eq);
  Op_ALU op_alu_1 (
    .add(add), .addi(addi), .sub(sub), .mult(mult), .mulu(mulu), .div(div), .divu(divu), .\and (\and ),
    .andi(andi), .\or (\or ), .ori(ori), .\nor (\nor ), .\xor (\xor ), .xori(xori), .slt(slt), .slti(slti),
    .sltu(sltu), .sltiu(sltiu), .out_19(out_3));
  // Probe on 6'b100100
  // Probe on 6'b100101
  // Probe on 6'b100111
  // Probe on 6'b101000
  // Probe on 6'b101010
  // Probe on 6'b101011
  Comparator #(.width(6)) comparator_7 (.a(in_1[5:0]), .b(6'b100100), .eq(comparator_7_eq));  // open: gt, lt
  Comparator #(.width(6)) comparator_8 (.a(in_1[5:0]), .b(6'b100101), .eq(comparator_8_eq));  // open: gt, lt
  Comparator #(.width(6)) comparator_9 (.a(in_1[5:0]), .b(6'b100111), .eq(comparator_9_eq));  // open: gt, lt
  Comparator #(.width(6)) comparator_10 (.a(in_1[5:0]), .b(6'b101000), .eq(comparator_10_eq));  // open: gt, lt
  Comparator #(.width(6)) comparator_11 (.a(in_1[5:0]), .b(6'b101010), .eq(comparator_11_eq));  // open: gt, lt
  Comparator #(.width(6)) comparator_12 (.a(in_1[5:0]), .b(6'b101011), .eq(comparator_12_eq));  // open: gt, lt
  Hi_Lo hi_lo_1 (.mult(mult), .mulu(mulu), .div(div), .divu(divu), .en_hi_lo(out_4));
  Constant_Extender_Selector constant_extender_selector_1 (.andi(andi), .ori(ori), .xori(xori), .out_4(out_19));
  and and_7 (\and , _0_op, comparator_7_eq);
  and and_8 (\or , _0_op, comparator_8_eq);
  and and_9 (\nor , _0_op, comparator_9_eq);
  and and_10 (\xor , _0_op, comparator_10_eq);
  and and_11 (slt, _0_op, comparator_11_eq);
  and and_12 (sltu, _0_op, comparator_12_eq);
  nor nor_1 (nor_1_out, en_jump, out_11, out_13);
  // Probe on 6'b001000
  // Probe on 6'b001100
  // Probe on 6'b001101
  // Probe on 6'b001110
  // Probe on 6'b001010
  // Probe on 6'b001011
  Type_I type_i_1 (
    .addi(addi), .slti(slti), .sltiu(sltiu), .const_ext(out_19), .lw(lw), .sw(save_word),
    .BC(BC_jump_Selector), .jr(jr), .out_9(out_21));
  Comparator #(.width(6)) comparator_13 (.a(in_1[31:26]), .b(6'b001000), .eq(addi));  // open: gt, lt
  Comparator #(.width(6)) comparator_14 (.a(in_1[31:26]), .b(6'b001100), .eq(andi));  // open: gt, lt
  Comparator #(.width(6)) comparator_15 (.a(in_1[31:26]), .b(6'b001101), .eq(ori));  // open: gt, lt
  Comparator #(.width(6)) comparator_16 (.a(in_1[31:26]), .b(6'b001110), .eq(xori));  // open: gt, lt
  Comparator #(.width(6)) comparator_17 (.a(in_1[31:26]), .b(6'b001010), .eq(slti));  // open: gt, lt
  Comparator #(.width(6)) comparator_18 (.a(in_1[31:26]), .b(6'b001011), .eq(sltiu));  // open: gt, lt
  // Probe on {6{1'b0}}
  RF_en rf_en_1 (
    .rnd(keyboard), .mfhi(rnd), .mflo(mfhi), .in_5(mflo), .nop(nop), .halt(Stop_program), .tty(out_23),
    .hi_lo(out_4), .out_10(out_7), .kbd(nor_1_out));
  Comparator #(.width(6)) comparator_19 (.a(in_1[31:26]), .b({6{1'b0}}), .eq(_0_op));  // open: gt, lt
  // Probe on 6'b000100
  // Probe on 6'b000101
  // Probe on 6'b000110
  // Probe on 6'b000111
  // Probe on 6'b000001
  // Probe on 6'b000010
  // Probe on 6'b001000
  // Probe on {6{1'b1}}
  Comparator #(.width(6)) comparator_20 (.a(in_1[31:26]), .b(6'b000100), .eq(beq));  // open: gt, lt
  Comparator #(.width(6)) comparator_21 (.a(in_1[31:26]), .b(6'b000101), .eq(bne));  // open: gt, lt
  Comparator #(.width(6)) comparator_22 (.a(in_1[31:26]), .b(6'b000110), .eq(blez));  // open: gt, lt
  Comparator #(.width(6)) comparator_23 (.a(in_1[31:26]), .b(6'b000111), .eq(bgtz));  // open: gt, lt
  Comparator #(.width(6)) comparator_24 (.a(in_1[31:26]), .b(6'b000001), .eq(bltz));  // open: gt, lt
  Comparator #(.width(6)) comparator_25 (.a(in_1[31:26]), .b(6'b000010), .eq(j));  // open: gt, lt
  and and_13 (jr, _0_op, comparator_26_eq);
  Comparator #(.width(6)) comparator_26 (.a(in_1[5:0]), .b(6'b001000), .eq(comparator_26_eq));  // open: gt, lt
  and and_14 (nop, _0_op, comparator_27_eq);
  Comparator #(.width(6)) comparator_27 (.a(in_1[5:0]), .b({6{1'b0}}), .eq(comparator_27_eq));  // open: gt, lt
  Jump jump_1 (.BC_select(BC_jump_Selector), .en_jump(en_jump));
  Branch_Control_Selector branch_control_selector_1 (
    .beq(beq), .bne(bne), .blez(blez), .bgtz(bgtz), .bltz(bltz), .j(j), .jr(jr), .out_8(Flag_Condition),
    .out_9(BC_jump_Selector));
  Comparator #(.width(6)) comparator_28 (.a(in_1[31:26]), .b({6{1'b1}}), .eq(_1_op));  // open: gt, lt
  // Probe on 6'b111000
  Comparator #(.width(6)) comparator_29 (.a(in_1[31:26]), .b(6'b100011), .eq(lw));  // open: gt, lt
  // Probe on 6'b100011
  Comparator #(.width(6)) comparator_30 (.a(in_1[31:26]), .b(6'b101011), .eq(save_word));  // open: gt, lt
  // Probe on 6'b101011
  Comparator #(.width(6)) comparator_31 (.a(in_1[31:26]), .b({6{1'b0}}), .eq(comparator_31_eq));  // open: gt, lt
  // Probe on {6{1'b0}}
  Comparator #(.width(6)) comparator_32 (.a(in_1[31:26]), .b(6'b000001), .eq(comparator_32_eq));  // open: gt, lt
  // Probe on 6'b000001
  Comparator #(.width(6)) comparator_33 (.a(in_1[5:0]), .b(6'b010000), .eq(comparator_33_eq));  // open: gt, lt
  // Probe on 6'b010000
  Comparator #(.width(6)) comparator_34 (.a(in_1[5:0]), .b(6'b010010), .eq(comparator_34_eq));  // open: gt, lt
  // Probe on 6'b010010
  Comparator #(.width(6)) comparator_35 (.a(in_1[31:26]), .b(6'b111000), .eq(stack_op));  // open: gt, lt
  and and_15 (pop, comparator_31_eq, stack_op);
  and and_16 (push, stack_op, comparator_32_eq);
  and and_17 (mfhi, _0_op, comparator_33_eq);
  and and_18 (mflo, _0_op, comparator_34_eq);
  or or_1 (out_11, lw, pop);
  or or_2 (out_13, save_word, push);
  RF_Input_Selector rf_input_selector_1 (
    .lw___pop(out_11), .rnd(rnd), .mfhi(mfhi), .mflo(mflo), .kbd(keyboard), .out_6(out_6));
  Memory_Address_Selector memory_address_selector_1 (
    .pop(pop), .push(push), .is_inst(in_2), .sw(save_word), .lw(lw), .out_6(out_9));
  // Probe on {6{1'b1}}
  // Probe on 6'b000001
  // Probe on 6'b000010
  // Probe on 6'b000100
  Comparator #(.width(6)) comparator_36 (.a(in_1[5:0]), .b({6{1'b1}}), .eq(comparator_36_eq));  // open: gt, lt
  Comparator #(.width(6)) comparator_37 (.a(in_1[5:0]), .b(6'b000001), .eq(comparator_37_eq));  // open: gt, lt
  Comparator #(.width(6)) comparator_38 (.a(in_1[5:0]), .b(6'b000010), .eq(comparator_38_eq));  // open: gt, lt
  Comparator #(.width(6)) comparator_39 (.a(in_1[5:0]), .b(6'b000100), .eq(comparator_39_eq));  // open: gt, lt
  and and_19 (Stop_program, _1_op, comparator_36_eq);
  and and_20 (out_23, _1_op, comparator_37_eq);
  and and_21 (rnd, _1_op, comparator_38_eq);
  and and_22 (keyboard, _1_op, comparator_39_eq);
  Multiplexer #(.width(5), .disabled(0), .enable("false")) multiplexer_1 (
    .in0(in_1[15:11]), .in1(in_1[20:16]), .out(out_10), .sel(out_21));

  assign out_14 = in_1[15:0];
  assign out_17 = in_1[25:0];
  assign Selector_A = in_1[25:21];
  assign Selector_B = in_1[20:16];

  // Other names for the same wires on the sheet: ALU_Op_select[3:0] = out_3; BC_select[1:0] = BC_jump_Selector;
  //   Data_Address[4:0] = out_10; en_Hi_Lo = out_4; extend = out_19; FC[2:0] = Flag_Condition; halt = Stop_program;
  //   const[15:0] = in_1[15:0]; Dest[25:0] = in_1[25:0]; Func_code[5:0] = in_1[5:0]; inst[31:0] = in_1;
  //   Rd[4:0] = in_1[15:11]; Rt[4:0] = in_1[20:16]; Rs[4:0] = in_1[25:21]; Op_code[5:0] = in_1[31:26]; is_inst = in_2;
  //   kbd = keyboard; MA_select[1:0] = out_9; Read_RAM = out_11; RF_en = out_7; RF_Select[2:0] = out_6;
  //   sw = save_word; tty = out_23; Type_I = out_21; Write_RAM = out_13

  // Notes on the sheet:
  //   Input
  //   ALU- Op
  //   INSTRUCTION DECODER
  //   Jump
  //   Memory
  //   Copy
  //   Especial
  //   Register File Input Selector
  //   ALU operation Selector
  //   Memory Address Input Selector
  //   EN constant extender
  //   Is Inmediate operation
  //   Output
  //   Is Hi-Lo operation
  //   Is read operation
  //   Is write operation
  //   Print instruction
  //   Data Address in Register File
  //   constant / offset
  //   Inconditional jump destination
endmodule

module Op_ALU (
  input  add,
  input  addi,
  input  sub,
  input  mult,
  input  mulu,
  input  div,
  input  divu,
  input  \and ,
  input  andi,
  input  \or ,
  input  ori,
  input  \nor ,
  input  \xor ,
  input  xori,
  input  slt,
  input  slti,
  input  sltu,
  input  sltiu,
  output [3:0] out_19
);

  wire add_t, and_t, or_t, priority_encoder_1_gs, slt_t, sltu_t, xor_t;
  wire [3:0] priority_encoder_1_out;

  or or_1 (add_t, add, addi);
  or or_2 (and_t, \and , andi);
  or or_3 (or_t, \or , ori);
  or or_4 (xor_t, \xor , xori);
  or or_5 (slt_t, slt, slti);
  or or_6 (sltu_t, sltu, sltiu);
  Priority_Encoder #(.select(4), .disabled(0)) priority_encoder_1 (
    .in0(add_t), .in1(sub), .in2(slt_t), .in3(sltu_t), .in4(and_t), .in5(or_t), .in6(\nor ), .in7(xor_t),
    .in8(mult), .in9(mulu), .in10(div), .in11(divu), .out(priority_encoder_1_out), .gs(priority_encoder_1_gs));  // open: in12, in13, in14, in15, en_out, en_in
  Multiplexer #(.width(4), .enable("false")) multiplexer_1 (
    .in0(4'b0000), .in1(priority_encoder_1_out), .out(out_19), .sel(priority_encoder_1_gs));

  // Other names for the same wires on the sheet: ALU_Op[3:0] = out_19

  // Notes on the sheet:
  //   Input
  //   ALU-Op
  //   Output
endmodule

module Hi_Lo (
  input  mult,
  input  mulu,
  input  div,
  input  divu,
  output en_hi_lo
);

  or or_1 (en_hi_lo, mult, mulu, div, divu);

  // Notes on the sheet:
  //   Hi-Lo
endmodule

module Jump (
  input  [1:0] BC_select,
  output en_jump
);

  or or_1 (en_jump, BC_select[0], BC_select[1]);

  // Notes on the sheet:
  //   Jump
endmodule

module Constant_Extender_Selector (
  input  andi,
  input  ori,
  input  xori,
  output out_4
);

  or or_1 (out_4, andi, ori, xori);

  // Notes on the sheet:
  //   To Extend
  //   Contant-Extender-Selector
endmodule

module Branch_Control_Selector (
  input  beq,
  input  bne,
  input  blez,
  input  bgtz,
  input  bltz,
  input  j,
  input  jr,
  output [2:0] out_8,
  output [1:0] out_9
);

  wire Branch;
  wire [2:0] priority_encoder_1_out;

  Priority_Encoder priority_encoder_1 (
    .in0(beq), .in1(bne), .in2(bgtz), .in3(blez), .in4(bltz), .out(priority_encoder_1_out), .en_in(1'b1),
    .gs(Branch));  // open: in5, in6, in7, en_out
  or or_1 (out_9[0], Branch, jr);
  or or_2 (out_9[1], jr, j);
  Multiplexer #(.width(3), .disabled(0), .enable("false")) multiplexer_1 (
    .in0(3'b000), .in1(priority_encoder_1_out), .out(out_8), .sel(Branch));

  // Other names for the same wires on the sheet: Flag_Condition[2:0] = out_8; selector[1:0] = out_9

  // Notes on the sheet:
  //   Input
  //   Branch Control
  //   Selector
  //   Output
endmodule

module RF_Input_Selector (
  input  lw___pop,
  input  mfhi,
  input  mflo,
  input  rnd,
  input  kbd,
  output [2:0] out_6
);

  wire priority_encoder_1_gs;
  wire [2:0] priority_encoder_1_out;

  Priority_Encoder priority_encoder_1 (
    .in1(lw___pop), .in2(mfhi), .in3(mflo), .in4(rnd), .in5(kbd), .out(priority_encoder_1_out), .en_in(1'b1),
    .gs(priority_encoder_1_gs));  // open: in0, in6, in7, en_out
  Multiplexer #(.width(3), .disabled(0), .enable("false")) multiplexer_1 (
    .in0(3'b000), .in1(priority_encoder_1_out), .out(out_6), .sel(priority_encoder_1_gs));

  // Other names for the same wires on the sheet: RAM = lw___pop; RF_Input_Select[2:0] = out_6

  // Notes on the sheet:
  //   Input
  //   RF Input
  //   Selector
  //   Output
endmodule

module Type_I (
  input  addi,
  input  slti,
  input  sltiu,
  input  const_ext,
  input  lw,
  input  sw,
  input  jr,
  input  [1:0] BC,
  output out_9
);

  wire and_1_out, or_1_out;

  and and_1 (and_1_out, ~jr, BC[0]);  // AND_Gate
  or or_1 (or_1_out, addi, slti, sltiu, const_ext, lw, sw);
  or or_2 (out_9, or_1_out, and_1_out);

  // Notes on the sheet:
  //   Type - I
endmodule

module Memory_Address_Selector (
  input  pop,
  input  push,
  input  is_inst,
  input  sw,
  input  lw,
  output [1:0] out_6
);

  or or_1 (out_6[1], pop, is_inst, push);
  or or_2 (out_6[0], sw, is_inst, lw);

  // Notes on the sheet:
  //   Input Selector
  //   Memory Address
endmodule

module RF_en (
  input  kbd,
  input  rnd,
  input  mfhi,
  input  mflo,
  input  in_5,
  input  nop,
  input  halt,
  input  tty,
  input  hi_lo,
  output out_10
);

  wire nor_1_out, or_1_out;

  or or_1 (or_1_out, kbd, rnd, mfhi, mflo, in_5);
  nor nor_1 (nor_1_out, nop, halt, tty, hi_lo);
  and and_1 (out_10, or_1_out, nor_1_out);

  // Notes on the sheet:
  //   no write, read, jump
  //   RF-en
endmodule
