// Logisim project Instruction Memory.circ as structural Verilog: 1 circuit, main circuit Instruction Memory
module Instruction_Memory (
  input  [31:0] in_1,
  input  en,
  input  clk,
  input  reset,
  output [31:0] out_5
);

  Register #(.width(32)) register_1 (.D(in_1), .en(en), .Q(out_5), .clk(clk), .clr(reset));

  // Notes on the sheet:
  //   Input
  //    Memory
  //   Instruction
  //   Output
endmodule
