// Logisim project Memory Address.circ as structural Verilog: 1 circuit, main circuit Memory Address
module Memory_Address (
  input  [31:0] in_1,
  input  [31:0] in_2,
  input  [31:0] in_3,
  input  [1:0] in_4,
  input  in_5,
  output [31:0] out_6
);

  wire [31:0] multiplexer_1_out, subtractor_1_out;

  Subtractor #(.width(32)) subtractor_1 (.a(in_2), .b(32'h4), .out(subtractor_1_out));  // open: bin, bout
  Multiplexer #(.width(32), .disabled(0), .enable("false")) multiplexer_1 (
    .in0(in_2), .in1(subtractor_1_out), .out(multiplexer_1_out), .sel(in_5));
  Multiplexer #(.select(2), .width(32), .disabled(0), .enable("false")) multiplexer_2 (
    .in0(in_1), .in1(multiplexer_1_out), .in2(in_3), .out(out_6), .sel(in_4));  // open: in3

  // Other names for the same wires on the sheet: ALU[31:0] = in_1; PC[31:0] = in_3; push = in_5;
  //   RAM_dir[31:0] = out_6; selector[1:0] = in_4; SP[31:0] = in_2

  // Notes on the sheet:
  //   Memory Address
endmodule
