// Logisim project Program Counter.circ as structural Verilog: 1 circuit, main circuit Program Counter
module Program_Counter (
  input  in_1,
  input  in_2,
  input  [31:0] in_3,
  input  in_4,
  output [31:0] out_5
);

  Register #(.width(32)) register_1 (.D(in_3), .en(in_1), .Q(out_5), .clk(in_2), .clr(in_4));

  // Other names for the same wires on the sheet: clk = in_2; en = in_1; reset = in_4

  // Notes on the sheet:
  //   Input
  //   Program Counter
  //   Output
endmodule
