// Logisim project RAM Interaction.circ as structural Verilog: 5 circuits, main circuit Timer
module Ram_Interaction (
  input  [31:0] in_1,
  input  [31:0] in_2,
  input  [31:0] in_3,
  input  [31:0] in_4,
  input  [31:0] in_5,
  input  [31:0] in_6,
  input  [3:0] in_7,
  input  [3:0] in_8,
  input  in_9,
  input  in_10,
  input  in_11,
  input  in_12,
  output [31:0] out_13,
  output [31:0] out_14,
  output [31:0] out_15,
  output [31:0] out_16,
  output [31:0] out_17,
  output [15:0] out_18,
  output [3:0] out_19,
  output out_20,
  output out_21,
  output out_22,
  output out_23
);

  wire CSR;

  Demultiplexer #(.select(2), .disabled(0), .enable("false")) demultiplexer_1 (
    .out0(out_19[0]), .out1(out_19[1]), .out2(out_19[2]), .out3(out_19[3]), .in(1'b1), .sel(in_5[3:2]));
  Read_RAM read_ram_1 (
    .in_1(in_1), .in_2(in_2), .in_3(in_3), .in_4(in_4), .in_5(in_5), .in_6(in_7), .in_7(in_10), .in_8(in_9),
    .in_9(in_11), .out_12(out_22), .out_11(CSR), .out_10(out_17));
  Write_RAM write_ram_1 (
    .in_1(in_5), .in_2(in_6), .in_3(in_8), .in_4(in_10), .in_5(in_9), .in_6(in_12), .out_7(out_13),
    .out_8(out_14), .out_9(out_15), .out_10(out_16), .out_12(out_23), .out_11(out_21));
  or or_1 (out_20, CSR, out_21);

  assign out_18 = in_5[19:4];

  // Other names for the same wires on the sheet: clk = in_10; CS = out_20; Data_Input[31:0] = in_6;
  //   Data_Output[31:0] = out_17; get_data = in_11; mask[3:0] = out_19; R_W = out_21; RAM_dir[31:0] = in_5;
  //   address[15:0] = in_5[19:4]; read_ready = out_22; read_time[3:0] = in_7; reset = in_9; RI0[31:0] = out_13;
  //   RI1[31:0] = out_14; RI2[31:0] = out_15; RI3[31:0] = out_16; RO0[31:0] = in_1; RO1[31:0] = in_2;
  //   RO2[31:0] = in_3; RO3[31:0] = in_4; write_data = in_12; write_ready = out_23; write_time[3:0] = in_8
endmodule

module Timer (
  input  start,
  input  clock,
  input  reset,
  input  [3:0] wait_time,
  output out_5
);

  wire [3:0] counter_1_q;

  Counter #(.width(4), .max('hf)) counter_1 (
    .count(start), .Q(counter_1_q), .clk(clock), .clr(reset));  // open: load, D, carry
  Comparator #(.width(4)) comparator_1 (.a(wait_time), .b(counter_1_q), .eq(out_5));  // open: gt, lt

  // Other names for the same wires on the sheet: clk = clock; ready = out_5

  // Notes on the sheet:
  //   Timer
endmodule

module Little_Endian (
  input  [31:0] in_1,
  output [31:0] out_2
);


  assign out_2 = {in_1[7:0], in_1[15:8], in_1[23:16], in_1[31:24]};

  // Notes on the sheet:
  //   Reverse Bytes
endmodule

module Read_RAM (
  input  [31:0] in_1,
  input  [31:0] in_2,
  input  [31:0] in_3,
  input  [31:0] in_4,
  input  [31:0] in_5,
  input  [3:0] in_6,
  input  in_7,
  input  in_8,
  input  in_9,
  output [31:0] out_10,
  output out_11,
  output out_12
);

  wire demultiplexer_1_out0, demultiplexer_1_out1, or_1_out, or_2_out, ready;
  wire [31:0] little_endian_1_out_2, multiplexer_1_out;

  or or_1 (or_1_out, demultiplexer_1_out0, in_9);
  or or_2 (or_2_out, out_12, in_8);
  D_Flip_Flop d_ff_1 (.clk(in_7), .D(or_1_out), .Q(out_11), .reset(in_8));  // open: Qn, preset, en
  Demultiplexer #(.disabled(0), .enable("false")) demultiplexer_1 (
    .out0(demultiplexer_1_out0), .out1(demultiplexer_1_out1), .in(out_11), .sel(ready));
  Multiplexer #(.select(2), .width(32), .disabled(0), .enable("false")) multiplexer_1 (
    .in0(in_1), .in1(in_2), .in2(in_3), .in3(in_4), .out(multiplexer_1_out), .sel(in_5[3:2]));
  Timer timer_1 (.start(out_11), .clock(in_7), .reset(or_2_out), .wait_time(in_6), .out_5(ready));
  Little_Endian little_endian_1 (.in_1(multiplexer_1_out), .out_2(little_endian_1_out_2));
  D_Flip_Flop d_ff_2 (.clk(in_7), .D(demultiplexer_1_out1), .Q(out_12), .reset(in_8));  // open: Qn, preset, en
  Register #(.width(32)) register_1 (.D(little_endian_1_out_2), .en(out_11), .Q(out_10), .clk(in_7), .clr(in_8));

  // Other names for the same wires on the sheet: Bank_0[31:0] = in_1; Bank_1[31:0] = in_2; Bank_2[31:0] = in_3;
  //   Bank_3[31:0] = in_4; clk = in_7; CS = out_11; Data_Out[31:0] = out_10; data_ready = out_12; get_data = in_9;
  //   RAM_dir[31:0] = in_5; selector[1:0] = in_5[3:2]; read_time[3:0] = in_6; reset = in_8
endmodule

module Write_RAM (
  input  [31:0] in_1,
  input  [31:0] in_2,
  input  [3:0] in_3,
  input  in_4,
  input  in_5,
  input  in_6,
  output [31:0] out_7,
  output [31:0] out_8,
  output [31:0] out_9,
  output [31:0] out_10,
  output out_11,
  output out_12
);

  wire demultiplexer_1_out0, demultiplexer_1_out1, or_1_out, or_2_out, ready;
  wire [31:0] little_endian_1_out_2;

  or or_1 (or_1_out, demultiplexer_1_out0, in_6);
  or or_2 (or_2_out, out_12, in_5);
  D_Flip_Flop d_ff_1 (.clk(in_4), .D(or_1_out), .Q(out_11), .reset(in_5));  // open: Qn, preset, en
  Little_Endian little_endian_1 (.in_1(in_2), .out_2(little_endian_1_out_2));
  Demultiplexer #(.disabled(0), .enable("false")) demultiplexer_1 (
    .out0(demultiplexer_1_out0), .out1(demultiplexer_1_out1), .in(out_11), .sel(ready));
  Demultiplexer #(.select(2), .width(32), .disabled(0), .enable("false")) demultiplexer_2 (
    .out0(out_7), .out1(out_8), .out2(out_9), .out3(out_10), .in(little_endian_1_out_2), .sel(in_1[3:2]));
  Timer timer_1 (.start(out_11), .clock(in_4), .reset(or_2_out), .wait_time(in_3), .out_5(ready));
  D_Flip_Flop d_ff_2 (.clk(in_4), .D(demultiplexer_1_out1), .Q(out_12), .reset(in_5));  // open: Qn, preset, en

  // Other names for the same wires on the sheet: Bank_0[31:0] = out_7; Bank_1[31:0] = out_8; Bank_2[31:0] = out_9;
  //   Bank_3[31:0] = out_10; clk = in_4; Data_Input[31:0] = in_2; R_W = out_11; RAM_dir[31:0] = in_1;
  //   selector[1:0] = in_1[3:2]; reset = in_5; write_data = in_6; write_ready = out_12; write_time[3:0] = in_3
endmodule
