// Logisim project Register File Input.circ as structural Verilog: 1 circuit, main circuit Register File Input
module Register_File_Input (
  input  [2:0] RF_Selector,
  input  [31:0] in_2,
  input  in_3,
  input  [31:0] in_4,
  input  [31:0] in_5,
  input  [31:0] in_6,
  input  [6:0] Keyboard,
  input  in_8,
  output [31:0] out_9
);

  wire [31:0] kbd_in, random;

  Random #(.width(32)) random_1 (.clk(in_3), .out(random));  // open: next, clr
  Multiplexer #(.width(32), .disabled(0), .enable("false")) multiplexer_1 (
    .in0({32{1'b1}}), .in1({{25{1'b0}}, Keyboard}), .out(kbd_in), .sel(in_8));
  Multiplexer #(.select(3), .width(32), .disabled(0), .enable("false")) multiplexer_2 (
    .in0(in_2), .in1(in_4), .in2(in_5), .in3(in_6), .in4(random), .in5(kbd_in), .out(out_9), .sel(RF_Selector));  // open: in6, in7

  // Other names for the same wires on the sheet: kbd[6:0] = Keyboard; ALU[31:0] = in_2; clk = in_3; Hi[31:0] = in_5;
  //   kbd_available = in_8; Lo[31:0] = in_6; RAM[31:0] = in_4; RF_Input[31:0] = out_9; Selector[2:0] = RF_Selector

  // Notes on the sheet:
  //   Low
  //   ALU Output
  //   RAM Output
  //   High
  //   keyboard available
  //   Input
  //   Register File Input
  //   Output
  //   Register File Input
endmodule
